# Fritzing sketch TriSpeed_MotorX (saved by Fritzing 1.0.5)
breadboards: 1

parts:
  Arduino_Uno_R3 = Arduino Uno (Rev3) - ICSP
  LED2 = LED - 3mm [color="White (6500K)" current=0.030A package="3 mm [THT]"]
  L298N1 = L298N DC motor driver
  6xAA_Battery1 = 6xAA Battery
  DC_Motor(F130_Type) = DC Motor [voltage_(max)=6V voltage_(min)=3V]  # not connected
  S1 = Pushbutton [package="[SMD]"]
  S2 = Pushbutton [package="[SMD]"]
  C2 = Ceramic Capacitor [capacitance=0.1µF voltage=35V package="200 mil [THT, multilayer]"]
  C3 = Ceramic Capacitor [capacitance=0.1µF voltage=35V package="200 mil [THT, multilayer]"]
  R2 = Resistor [tolerance=±1% power=0.25W resistance=10k package=THT]
  R3 = Resistor [tolerance=±1% power=0.25W resistance=10k package=THT]
  R4 = Resistor [tolerance=±1% power=0.25W resistance=2.2k package=THT]
  R5 = Resistor [tolerance=±1% power=0.25W resistance=1k package=THT]
  SSD1306 = OLED 128x64 I2C Monochrome Display
  HW-479 = RGB LED (com. cathode, rgb) [color="Red (633nm)" current=0.030A package="5 mm [THT]"]
  R1 = Resistor [tolerance=±5% resistance=330 package="1206 [SMD]"]

nets (from the breadboard view):
  N1: Arduino_Uno_R3.D9_PWM, HW-479.blue_anode
  N2: Arduino_Uno_R3.D1/TX, R5.Pin_0
  N3: Arduino_Uno_R3.D3_PWM, R1.Pin_1
  N4: Arduino_Uno_R3.D5_PWM, HW-479.red_anode
  N5: Arduino_Uno_R3.D6_PWM, HW-479.green_anode
  GND: Arduino_Uno_R3.GND, LED2.cathode, L298N1.GND, L298N1.IN2, 6xAA_Battery1.Pin_1, S1.Pin_3, S1.Pin_4, S2.Pin_3, S2.Pin_4, C2.1, C3.1, R4.Pin_1, SSD1306.GND, HW-479.common_cathode
  N6: LED2.anode, R1.Pin_0
  N7: L298N1.12V, 6xAA_Battery1.Pin_2
  N8: S1.Pin_1, S1.Pin_2, C2.0, R2.Pin_0
  N9: S2.Pin_1, S2.Pin_2, C3.0, R3.Pin_0
  N10: R4.Pin_0, R5.Pin_1

notes:
  ENA to STM32 PA6
  IN1 to STM32 PB12
  Button 1 to STM32 PB13
  Button 2 to STM32 PB14
  To STM32 PA10(RX)
  To STM32 PA9(TX)
  SCL to STM32 PB8
  SDA to STM32 PB9
  +3V3 from STM32
  GND from STM32

custom parts:
  L298N DC motor driver: 2x DC motor driver with 78M05 positive voltage regulator (7..35 V) L298N: max 46 V, 2 A Set 5 V Enable jumper to enable 5 V regultor (needed for the L298N) and +5 V output at screw terminal or supply external +5 V at screw terminal Set ENA and/or ENB to +5 V to enable motor permanently or supply ENA and/or ENB with PWM signal IN1 and IN2 set rotation directory for motor A (OUT1/OUT2) IN2 and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
  6xAA Battery: 6xAA battery

// code stored in the sketch: TriSpeed_MotorX.ino
#define RED_PIN     5
#define GREEN_PIN   6
#define BLUE_PIN    9
#define WHITE_PIN   3
//#define BTN1_PIN    7


bool settingMode = false;
int speedMode = 0;  // 0=???1=??2=??3=?


void setup() {
  pinMode(RED_PIN, OUTPUT);
  pinMode(GREEN_PIN, OUTPUT);
  pinMode(BLUE_PIN, OUTPUT);
  pinMode(WHITE_PIN, OUTPUT);
  //pinMode(BTN1_PIN, INPUT_PULLUP);


  Serial.begin(115200);
}


void loop() {
  handleSerial();
  //handleButton();


  if (settingMode) {
    blinkWhiteLED();
    showSettingRGB();
  } else {
    digitalWrite(WHITE_PIN, LOW);
    showNormalRGB();
  }
}


void handleSerial() {
  if (Serial.available()) {
    char ch = Serial.read();
    if (ch == 's') {
      settingMode = true;
      speedMode = 0;
    } else if (ch == 'e') {
      settingMode = false;
    } else if (ch >= '0' && ch <= '3') {
      speedMode = ch - '0';
    }
  }
}


/*void handleButton() {
  static unsigned long lastBtnTime = 0;
  if (!settingMode && digitalRead(BTN1_PIN) == LOW) {
    if (millis() - lastBtnTime > 300) {
      speedMode++;
      if (speedMode > 3) speedMode = 0;
      lastBtnTime = millis();
    }
  }
}*/


void blinkWhiteLED() {
  static unsigned long lastToggle = 0;
  static bool ledState = false;
  if (millis() - lastToggle > 500) {
    ledState = !ledState;
    digitalWrite(WHITE_PIN, ledState);
    lastToggle = millis();
  }
}


void showNormalRGB() {
  switch (speedMode) {
    case 0: warmBreathing(); break;
    case 1: rgb(0, 255, 0); break;      // ?
    case 2: rgb(255, 255, 0); break;    // ?
    case 3: rgb(255, 0, 0); break;      // ?
  }
}


void showSettingRGB() {
  static unsigned long lastToggle = 0;
  static bool flashState = false;
  static int breath = 0;
  static int delta = 2;


  if (speedMode == 0) {
    if (millis() - lastToggle > 15) {
      breath += delta;
      if (breath > 255 || breath < 0) delta = -delta;
      breath = constrain(breath, 0, 255);
      rgb(breath / 2, 0, breath);  // ?????
      lastToggle = millis();
    }
  } else {
    if (millis() - lastToggle > 300) {
      flashState = !flashState;
      lastToggle = millis();
    }
    if (flashState) {
      switch (speedMode) {
        case 1: rgb(0, 255, 0); break;
        case 2: rgb(255, 255, 0); break;
        case 3: rgb(255, 0, 0); break;
      }
    } else {
      rgb(0, 0, 0);
    }
  }
}


void warmBreathing() {
  static unsigned long lastTime = 0;
  static int b = 0;
  static int delta = 2;


  if (millis() - lastTime > 15) {
    b += delta;
    if (b > 255 || b < 0) delta = -delta;
    b = constrain(b, 0, 255);
    rgb(b, b / 4, 0);  // ????
    lastTime = millis();
  }
}


void rgb(int r, int g, int b) {
  analogWrite(RED_PIN, r);
  analogWrite(GREEN_PIN, g);
  analogWrite(BLUE_PIN, b);
}
